// Logisim project control_logic.circ as structural Verilog: 1 circuit, main circuit control_logic
module control_logic (
  input  [31:0] inst,
  input  BrEq,
  input  BrLt,
  output PCSel,
  output RegWEn,
  output [2:0] ImmSel,
  output BrUn,
  output ASel,
  output BSel,
  output [3:0] ALUSel,
  output MemRW,
  output [1:0] WBSel
);

  wire add, and_r, auipc, bsel_t, comparator_1_eq, comparator_4_eq, comparator_5_eq, comparator_9_eq,
       comparator_11_eq, comparator_12_eq, comparator_13_eq, comparator_14_eq, comparator_15_eq,
       comparator_16_eq, comparator_17_eq, comparator_18_eq, comparator_19_eq, comparator_20_eq,
       comparator_21_eq, comparator_22_eq, comparator_23_eq, comparator_25_eq, comparator_26_eq,
       comparator_27_eq, comparator_28_eq, comparator_29_eq, comparator_30_eq, comparator_31_eq,
       comparator_32_eq, comparator_33_eq, comparator_34_eq, comparator_35_eq, comparator_36_eq,
       comparator_37_eq, comparator_38_eq, comparator_39_eq, comparator_40_eq, comparator_41_eq, divu, I,
       jalr, lw3, mul, mulh, mulhu, nothing, or_r, R, remu, S, SB, sll_r, slt, sra_r, srl_r, sub, U, xor_r;
  wire [2:0] multiplexer_2_out, multiplexer_4_out, multiplexer_6_out;
  wire [3:0] multiplexer_1_out, multiplexer_3_out, multiplexer_5_out, multiplexer_7_out, multiplexer_8_out,
       multiplexer_10_out, multiplexer_11_out, multiplexer_12_out, multiplexer_13_out, multiplexer_14_out,
       multiplexer_15_out, multiplexer_16_out, multiplexer_17_out, multiplexer_18_out;

  Comparator #(.width(3)) comparator_1 (.a(inst[14:12]), .b(3'b101), .eq(comparator_1_eq));  // open: gt, lt
  Comparator #(.width(7)) comparator_2 (.a(inst[6:0]), .b(7'b0110011), .eq(R));  // open: gt, lt
  Comparator #(.width(7)) comparator_3 (.a(inst[6:0]), .b(7'b0000011), .eq(lw3));  // open: gt, lt
  Comparator #(.width(7)) comparator_4 (.a(inst[6:0]), .b(7'b0010011), .eq(comparator_4_eq));  // open: gt, lt
  Comparator #(.width(3)) comparator_5 (.a(inst[14:12]), .b(3'b000), .eq(comparator_5_eq));  // open: gt, lt
  Comparator #(.width(7)) comparator_6 (.a(inst[6:0]), .b(7'b0100011), .eq(S));  // open: gt, lt
  Comparator #(.width(7)) comparator_7 (.a(inst[6:0]), .b(7'b1100011), .eq(SB));  // open: gt, lt
  Comparator #(.width(7)) comparator_8 (.a(inst[6:0]), .b(7'b0010111), .eq(auipc));  // open: gt, lt
  Comparator #(.width(7)) comparator_9 (.a(inst[6:0]), .b(7'b0110111), .eq(comparator_9_eq));  // open: gt, lt
  Comparator #(.width(7)) comparator_10 (.a(inst[6:0]), .b(7'b1101111), .eq(WBSel[1]));  // open: gt, lt
  Comparator #(.width(7)) comparator_11 (.a(inst[31:25]), .b({7{1'b0}}), .eq(comparator_11_eq));  // open: gt, lt
  Comparator #(.width(3)) comparator_12 (.a(inst[14:12]), .b(3'b000), .eq(comparator_12_eq));  // open: gt, lt
  Comparator #(.width(7)) comparator_13 (.a(inst[31:25]), .b(7'b0000001), .eq(comparator_13_eq));  // open: gt, lt
  Comparator #(.width(3)) comparator_14 (.a(inst[14:12]), .b(3'b000), .eq(comparator_14_eq));  // open: gt, lt
  Comparator #(.width(7)) comparator_15 (.a(inst[31:25]), .b(7'b0100000), .eq(comparator_15_eq));  // open: gt, lt
  Comparator #(.width(3)) comparator_16 (.a(inst[14:12]), .b(3'b000), .eq(comparator_16_eq));  // open: gt, lt
  Comparator #(.width(7)) comparator_17 (.a(inst[31:25]), .b({7{1'b0}}), .eq(comparator_17_eq));  // open: gt, lt
  Comparator #(.width(3)) comparator_18 (.a(inst[14:12]), .b(3'b100), .eq(comparator_18_eq));  // open: gt, lt
  Comparator #(.width(7)) comparator_19 (.a(inst[31:25]), .b(7'b0000001), .eq(comparator_19_eq));  // open: gt, lt
  Comparator #(.width(3)) comparator_20 (.a(inst[14:12]), .b(3'b101), .eq(comparator_20_eq));  // open: gt, lt
  Comparator #(.width(7)) comparator_21 (.a(inst[31:25]), .b({7{1'b0}}), .eq(comparator_21_eq));  // open: gt, lt
  Comparator #(.width(7)) comparator_22 (.a(inst[31:25]), .b({7{1'b0}}), .eq(comparator_22_eq));  // open: gt, lt
  Comparator #(.width(3)) comparator_23 (.a(inst[14:12]), .b(3'b111), .eq(comparator_23_eq));  // open: gt, lt
  Comparator #(.width(7)) comparator_24 (.a(7'b0110111), .b(inst[6:0]), .eq(bsel_t));  // open: gt, lt
  Comparator #(.width(7)) comparator_25 (.a(inst[6:0]), .b(7'b1100111), .eq(comparator_25_eq));  // open: gt, lt
  and and_1 (srl_r, comparator_21_eq, comparator_1_eq, R);
  and and_2 (and_r, comparator_22_eq, comparator_23_eq, R);
  and and_3 (jalr, comparator_25_eq, comparator_5_eq);
  or or_1 (U, auipc, comparator_9_eq);
  and and_4 (add, comparator_11_eq, comparator_12_eq, R);
  and and_5 (mul, comparator_13_eq, comparator_14_eq, R);
  and and_6 (sub, comparator_15_eq, comparator_16_eq, R);
  and and_7 (xor_r, comparator_17_eq, comparator_18_eq, R);
  and and_8 (divu, comparator_19_eq, comparator_20_eq, R);
  or or_2 (I, lw3, comparator_4_eq, jalr);
  Comparator #(.width(7)) comparator_26 (.a(inst[31:25]), .b({7{1'b0}}), .eq(comparator_26_eq));  // open: gt, lt
  Comparator #(.width(3)) comparator_27 (.a(inst[14:12]), .b(3'b001), .eq(comparator_27_eq));  // open: gt, lt
  Comparator #(.width(3)) comparator_28 (.a(inst[14:12]), .b(3'b001), .eq(comparator_28_eq));  // open: gt, lt
  Comparator #(.width(3)) comparator_29 (.a(inst[14:12]), .b(3'b011), .eq(comparator_29_eq));  // open: gt, lt
  Comparator #(.width(3)) comparator_30 (.a(inst[14:12]), .b(3'b010), .eq(comparator_30_eq));  // open: gt, lt
  Comparator #(.width(3)) comparator_31 (.a(inst[14:12]), .b(3'b101), .eq(comparator_31_eq));  // open: gt, lt
  Comparator #(.width(3)) comparator_32 (.a(inst[14:12]), .b(3'b110), .eq(comparator_32_eq));  // open: gt, lt
  Multiplexer #(.width(4), .enable("false")) multiplexer_1 (
    .in0(4'b0000), .in1(4'b0001), .out(multiplexer_1_out), .sel(and_r));
  Multiplexer #(.width(3), .enable("false")) multiplexer_2 (
    .in0(3'b000), .in1(3'b001), .out(multiplexer_2_out), .sel(S));
  Comparator #(.width(7)) comparator_33 (.a(inst[31:25]), .b(7'b0000001), .eq(comparator_33_eq));  // open: gt, lt
  Comparator #(.width(7)) comparator_34 (.a(inst[31:25]), .b(7'b0000001), .eq(comparator_34_eq));  // open: gt, lt
  Comparator #(.width(7)) comparator_35 (.a(inst[31:25]), .b({7{1'b0}}), .eq(comparator_35_eq));  // open: gt, lt
  Comparator #(.width(7)) comparator_36 (.a(inst[31:25]), .b(7'b0100000), .eq(comparator_36_eq));  // open: gt, lt
  Comparator #(.width(7)) comparator_37 (.a(inst[31:25]), .b({7{1'b0}}), .eq(comparator_37_eq));  // open: gt, lt
  Comparator #(.width(7)) comparator_38 (.a(inst[31:25]), .b(7'b0001111), .eq(comparator_38_eq));  // open: gt, lt
  Comparator #(.width(3)) comparator_39 (.a(inst[14:12]), .b(3'b000), .eq(comparator_39_eq));  // open: gt, lt
  Multiplexer #(.width(4), .enable("false")) multiplexer_3 (
    .in0(multiplexer_1_out), .in1(4'b0010), .out(multiplexer_3_out), .sel(or_r));
  Multiplexer #(.width(3), .enable("false")) multiplexer_4 (
    .in0(multiplexer_2_out), .in1(3'b010), .out(multiplexer_4_out), .sel(SB));
  and and_9 (sll_r, comparator_26_eq, comparator_27_eq, R);
  and and_10 (mulh, comparator_33_eq, comparator_28_eq, R);
  and and_11 (mulhu, comparator_34_eq, comparator_29_eq, R);
  and and_12 (slt, comparator_35_eq, comparator_30_eq, R);
  and and_13 (sra_r, comparator_36_eq, comparator_31_eq, R);
  and and_14 (or_r, comparator_37_eq, comparator_32_eq, R);
  not not_1 (BSel, R);
  Multiplexer #(.width(4), .enable("false")) multiplexer_5 (
    .in0(multiplexer_3_out), .in1(4'b0011), .out(multiplexer_5_out), .sel(xor_r));
  Multiplexer #(.width(3), .enable("false")) multiplexer_6 (
    .in0(multiplexer_4_out), .in1(3'b011), .out(multiplexer_6_out), .sel(U));
  and and_15 (nothing, comparator_38_eq, comparator_39_eq, R);
  Multiplexer #(.width(4), .enable("false")) multiplexer_7 (
    .in0(multiplexer_5_out), .in1(4'b0100), .out(multiplexer_7_out), .sel(srl_r));
  Multiplexer #(.width(4), .enable("false")) multiplexer_8 (
    .in0(multiplexer_7_out), .in1(4'b0101), .out(multiplexer_8_out), .sel(sra_r));
  Multiplexer #(.width(3), .enable("false")) multiplexer_9 (
    .in0(multiplexer_6_out), .in1(3'b100), .out(ImmSel), .sel(WBSel[1]));
  or or_3 (ASel, SB, auipc, WBSel[1]);
  Multiplexer #(.width(4), .enable("false")) multiplexer_10 (
    .in0(multiplexer_8_out), .in1(4'b0110), .out(multiplexer_10_out), .sel(sll_r));
  Comparator #(.width(7)) comparator_40 (.a(inst[31:25]), .b(7'b0000001), .eq(comparator_40_eq));  // open: gt, lt
  Comparator #(.width(3)) comparator_41 (.a(inst[14:12]), .b(3'b111), .eq(comparator_41_eq));  // open: gt, lt
  Multiplexer #(.width(4), .enable("false")) multiplexer_11 (
    .in0(multiplexer_10_out), .in1(4'b0111), .out(multiplexer_11_out), .sel(slt));
  Multiplexer #(.width(4), .enable("false")) multiplexer_12 (
    .in0(multiplexer_11_out), .in1(4'b1000), .out(multiplexer_12_out), .sel(divu));
  and and_16 (remu, comparator_40_eq, comparator_41_eq, R);
  or or_4 (WBSel[0], jalr, lw3);
  Multiplexer #(.width(4), .enable("false")) multiplexer_13 (
    .in0(multiplexer_12_out), .in1(4'b1001), .out(multiplexer_13_out), .sel(remu));
  Multiplexer #(.width(4), .enable("false")) multiplexer_14 (
    .in0(multiplexer_13_out), .in1(4'b1010), .out(multiplexer_14_out), .sel(mul));
  Multiplexer #(.width(4), .enable("false")) multiplexer_15 (
    .in0(multiplexer_14_out), .in1(4'b1011), .out(multiplexer_15_out), .sel(mulhu));
  Multiplexer #(.width(4), .enable("false")) multiplexer_16 (
    .in0(multiplexer_15_out), .in1(4'b1100), .out(multiplexer_16_out), .sel(sub));
  Multiplexer #(.width(4), .enable("false")) multiplexer_17 (
    .in0(multiplexer_16_out), .in1(4'b1101), .out(multiplexer_17_out), .sel(bsel_t));
  Multiplexer #(.width(4), .enable("false")) multiplexer_18 (
    .in0(multiplexer_17_out), .in1(4'b1110), .out(multiplexer_18_out), .sel(mulh));
  Multiplexer #(.width(4), .enable("false")) multiplexer_19 (
    .in0(multiplexer_18_out), .in1(4'b1111), .out(ALUSel), .sel(nothing));

  // Other names for the same wires on the sheet: opcode[6:0] = inst[6:0]; imm7_31[24:0] = inst[31:7];
  //   rd[4:0] = inst[11:7]; func3[2:0] = inst[14:12]; rs1[4:0] = inst[19:15]; rs2[4:0] = inst[24:20];
  //   func7[6:0] = inst[31:25]; UJ = WBSel[1]

  // Notes on the sheet:
  //   INPUTS to your circuit
  //   DON'T CHANGE THE LOCATIONS OF THE INPUTS AND OUTPUTS!
  //   OUTPUT from your circuit
endmodule
