// Logisim project cpu.circ as structural Verilog: 1 circuit, main circuit main
module main (
  input  [31:0] INSTRUCTION,
  input  CLOCK,
  output [31:0] PROGRAM_COUNTER,
  output [31:0] ra,
  output [31:0] sp,
  output [31:0] t0,
  output [31:0] t1,
  output [31:0] t2,
  output [31:0] s0,
  output [31:0] s1,
  output [31:0] a0
);

  wire BrEq, BrLt, RegWEn;
  wire [1:0] WBSel;
  wire [2:0] ImmSel;
  wire [3:0] ALUSel;
  wire [31:0] adder_1_out, immediate, RegFile_read_data_1, write_back;

  control_logic control_logic_1 (
    .ImmSel(ImmSel), .RegWEn(RegWEn), .BrLt(BrLt), .BrEq(BrEq), .inst(INSTRUCTION), .ALUSel(ALUSel),
    .WBSel(WBSel));  // open: BSel, ASel, BrUn, PCSel, MemRW
  Adder #(.width(32)) adder_1 (.a(PROGRAM_COUNTER), .b(32'h4), .out(adder_1_out));  // open: cin, cout
  Register #(.width(32)) PC (.D(adder_1_out), .clk(CLOCK), .Q(PROGRAM_COUNTER));  // open: en, clr
  imm_gen imm_gen_1 (.ImmSel(ImmSel), .inst(INSTRUCTION), .imm(immediate));
  branch_comp branch_comp_1 (.BrEq(BrEq), .BrLt(BrLt));  // open: BrUn, rs1, rs2
  regfile_main RegFile (
    .rs2(INSTRUCTION[19:15]), .rd(INSTRUCTION[11:7]), .Read_Data_1(RegFile_read_data_1), .ra(ra), .sp(sp),
    .t0(t0), .t1(t1), .t2(t2), .s0(s0), .s1(s1), .a0(a0), .rs1(INSTRUCTION[19:15]), .Write_Data(write_back),
    .RegWEn(1'b1), .clk(CLOCK));  // open: Read_Data_2
  alu Arithmetic_Logic_Unit (.Result(write_back), .ALUSel(4'b0000), .A(RegFile_read_data_1), .B(immediate));
  // mem_main DMEM: pin names not known

  // Other names for the same wires on the sheet: clk = CLOCK; opcode[6:0] = INSTRUCTION[6:0];
  //   imm7_31[24:0] = INSTRUCTION[31:7]; rd[4:0] = INSTRUCTION[11:7]; func3[2:0] = INSTRUCTION[14:12];
  //   rs1[4:0] = INSTRUCTION[19:15]; rs2[4:0] = INSTRUCTION[24:20]; func7[6:0] = INSTRUCTION[31:25]

  // Notes on the sheet:
  //   Output
  //   IMEM (do **NOT** move this)
  //   Inputs
  //   It is OK to move the PC, RegFile, ALU, MEM, Branch Comp, Imm Gen, and Control Logic to wherever is most convenient for you when constructing your CPU, and to delete this text
  //   Inputs/Outputs for testing. Do **NOT** move these.
endmodule
